// Logisim project Worder16.circ as structural Verilog: 2 circuits, main circuit main
module main (
);

  wire adder_1_cout, afs, and_1_out, and_2_out, and_3_out, and_4_out, and_5_out, and_6_out, and_7_out,
       and_8_out, and_9_out, and_10_out, as, be, bs, clock_1_out, counter_2_q, decoder_1_out0,
       decoder_1_out1, decoder_1_out2, decoder_2_out1, iare, iars, iope, iopi, mae, mas, mie, mis, moe, mos,
       ms, nor_1_out, not_1_out, or_2_out, or_3_out, or_8_out, p00, p01, p02, p03, p04, p05, p06, p07, pcc,
       pce, pci, pcs, pull_resistor_67_node, r1e, r1s, r2e, r2s, rar, raw, rse, rss, spc, spe, spi,
       subtractor_1_bout, xor_1_out;
  wire [3:0] controlled_buffer_1_out_3, controlled_buffer_3_out, controlled_buffer_4_out,
       controlled_buffer_25_out, controlled_buffer_25_out_2, controlled_buffer_25_out_3,
       controlled_buffer_25_out_4, counter_3_q, counter_5_q, rdw_q, rdw_q_2, rdw_q_3, rdw_q_4, rew_q,
       rew_q_2, rew_q_3, rew_q_4, rfw_q, rfw_q_2, rfw_q_3, rfw_q_4, rgw_q, rgw_q_2, rgw_q_3, rgw_q_4, rhw_q,
       rhw_q_2, rhw_q_3, rhw_q_4, riw_q, riw_q_2, riw_q_3, riw_q_4, rjw_q, rjw_q_2, rjw_q_3, rjw_q_4, rkw_q,
       rkw_q_2, rkw_q_3, rkw_q_4, rlw_q, rlw_q_2, rlw_q_3, rlw_q_4, rmw_q, rmw_q_2, rmw_q_3, rmw_q_4, rnw_q,
       rnw_q_2, rnw_q_3, rnw_q_4, rpw_q, rpw_q_2, rpw_q_3, rpw_q_4, rqw_q, rqw_q_2, rqw_q_3, rqw_q_4;
  wire [4:0] controlled_buffer_1_out, customcomparator_1_p8, ledbar_1_p1;
  wire [9:8] or_1_out;
  wire [10:5] controlled_buffer_1_out_2;
  wire [15:0] acc_q, adder_1_out, adder_2_out, alb_q, and_11_out, controlled_buffer_9_out,
       controlled_buffer_10_out, controlled_buffer_26_out, controlled_buffer_27_out,
       controlled_buffer_28_out, controlled_buffer_30_out, counter_4_q, decoder_2_out0, instr_test, muc_q,
       multiplier_1_cout, multiplier_1_out, not_2_out, or_6_out, or_9_out, pull_resistor_59_node, ram_1_dout,
       reg1_test, reg2_test, register_1_q, register_3_q, register_4_q, register_5_q, register_6_q,
       shifter_1_out, shifter_2_out, shifter_3_out, shifter_4_out, subtractor_1_out, subtractor_2_out,
       xor_2_out;
  wire [15:4] pull_resistor_84_node;

  Clock clock_1 (.out(clock_1_out));
  xor xor_1 (xor_1_out, clock_1_out, counter_2_q);
  and and_1 (and_1_out, counter_3_q[3], counter_3_q[2], counter_3_q[1], counter_3_q[0]);
  Counter #(.max('h1f), .trigger("falling"), .width(5)) counter_1 (
    .clr(1'b0), .load(1'b0), .up(1'b1), .count(1'b1), .clk(and_1_out), .Q(instr_test[15:11]));  // open: D, carry
  DipSwitch #(.number(16)) dipswitch_1 (
    .sw1(reg1_test[15]), .sw2(reg1_test[14]), .sw3(reg1_test[13]), .sw4(reg1_test[12]), .sw5(reg1_test[11]),
    .sw6(reg1_test[10]), .sw7(reg1_test[9]), .sw8(reg1_test[8]), .sw9(reg1_test[7]), .sw10(reg1_test[6]),
    .sw11(reg1_test[5]), .sw12(reg1_test[4]), .sw13(reg1_test[3]), .sw14(reg1_test[2]), .sw15(reg1_test[1]),
    .sw16(reg1_test[0]));
  Counter #(.max('h1), .trigger("falling"), .width(1)) counter_2 (
    .clr(1'b0), .load(1'b0), .up(1'b1), .count(1'b1), .clk(clock_1_out), .D(1'b0), .Q(counter_2_q));  // open: carry
  Counter #(.max('hf), .trigger("falling"), .width(4)) counter_3 (
    .clr(1'b0), .load(1'b0), .up(1'b1), .count(1'b1), .clk(counter_2_q), .Q(counter_3_q));  // open: D, carry
  and and_2 (and_2_out, ~counter_3_q[0], counter_3_q[1], ~counter_3_q[2], ~counter_3_q[3]);  // AND_Gate
  Register #(.trigger("high"), .width(16)) register_1 (
    .D(controlled_buffer_9_out), .en(and_2_out), .clk(xor_1_out), .Q(register_1_q));  // open: clr
  DipSwitch #(.number(11)) dipswitch_2 (
    .sw1(instr_test[10]), .sw2(instr_test[9]), .sw3(instr_test[8]), .sw4(instr_test[7]), .sw5(instr_test[6]),
    .sw6(instr_test[5]), .sw7(instr_test[4]), .sw8(instr_test[3]), .sw9(instr_test[2]), .sw10(instr_test[1]),
    .sw11(instr_test[0]));
  and and_3 (and_3_out, ~counter_3_q[0], ~counter_3_q[1], ~counter_3_q[2], ~counter_3_q[3]);  // AND_Gate
  and and_4 (and_4_out, counter_3_q[0], ~counter_3_q[1], ~counter_3_q[2], ~counter_3_q[3]);  // AND_Gate
  nor nor_1 (nor_1_out, and_3_out, and_4_out, and_5_out);
  assign {or_1_out[8], controlled_buffer_1_out_3, controlled_buffer_1_out_2, controlled_buffer_1_out} = nor_1_out ? register_1_q : 16'bz;  // Controlled_Buffer controlled_buffer_1
  not not_1 (not_1_out, nor_1_out);
  DipSwitch #(.number(16)) dipswitch_3 (
    .sw1(reg2_test[15]), .sw2(reg2_test[14]), .sw3(reg2_test[13]), .sw4(reg2_test[12]), .sw5(reg2_test[11]),
    .sw6(reg2_test[10]), .sw7(reg2_test[9]), .sw8(reg2_test[8]), .sw9(reg2_test[7]), .sw10(reg2_test[6]),
    .sw11(reg2_test[5]), .sw12(reg2_test[4]), .sw13(reg2_test[3]), .sw14(reg2_test[2]), .sw15(reg2_test[1]),
    .sw16(reg2_test[0]));
  and and_5 (and_5_out, ~counter_3_q[0], counter_3_q[1], ~counter_3_q[2], ~counter_3_q[3]);  // AND_Gate
  assign {or_1_out[8], controlled_buffer_1_out_3, controlled_buffer_1_out_2, controlled_buffer_1_out} = not_1_out ? {16{1'b0}} : 16'bz;  // Controlled_Buffer controlled_buffer_2
  Hex_Digit_Display #(.decimalPoint("false")) hex_digit_display_1 (.value(register_1_q[15:12]));
  LED led_1 (.in(counter_3_q[3]));
  Hex_Digit_Display #(.decimalPoint("false")) hex_digit_display_2 (.value(register_1_q[11:8]));
  Hex_Digit_Display #(.decimalPoint("false")) hex_digit_display_3 (.value(register_1_q[7:4]));
  LED led_2 (.in(counter_2_q));
  LED led_3 (.in(clock_1_out));
  LED led_4 (.in(counter_3_q[2]));
  LED led_5 (.in(counter_3_q[1]));
  LED led_6 (.in(counter_3_q[0]));
  and and_6 (and_6_out, ledbar_1_p1[0], controlled_buffer_1_out[0]);
  and and_7 (and_7_out, ledbar_1_p1[1], controlled_buffer_1_out[1]);
  and and_8 (and_8_out, ledbar_1_p1[2], controlled_buffer_1_out[2]);
  and and_9 (and_9_out, ledbar_1_p1[3], controlled_buffer_1_out[3]);
  and and_10 (and_10_out, ledbar_1_p1[4], controlled_buffer_1_out[4]);
  Hex_Digit_Display #(.decimalPoint("false")) hex_digit_display_4 (.value(register_1_q[3:0]));
  LED led_7 (.in(afs));
  LED led_8 (.in(ms));
  ROM #(.addrWidth(10)) Rom_MemoryControl (
    .addr({or_1_out, controlled_buffer_1_out_3, counter_3_q}), .data({moe, mos, mie, mis, mae, mas, raw, rar}));
  ROM #(.addrWidth(10), .dataWidth(10)) Rom_CounterControl (
    .addr({or_1_out, controlled_buffer_1_out_3, counter_3_q}),
    .data({afs, iare, iars, spe, spi, spc, pce, pcs, pci, pcc}));
  or or_1 (or_1_out[9], and_6_out, and_7_out, and_8_out, and_9_out, and_10_out);
  ROM #(.addrWidth(10), .dataWidth(10)) Rom_RegisterControl (
    .addr({or_1_out, controlled_buffer_1_out_3, counter_3_q}),
    .data({ms, as, be, bs, r2e, r2s, r1e, r1s, rse, rss}));
  ROM #(.addrWidth(10), .dataWidth(10)) Rom_PeripheralControl (
    .addr({or_1_out, controlled_buffer_1_out_3, counter_3_q}),
    .data({iope, iopi, p07, p06, p05, p04, p03, p02, p01, p00}));
  assign controlled_buffer_3_out = rss ? {controlled_buffer_1_out_2[7:5], controlled_buffer_1_out[4]} : 4'bz;  // Controlled_Buffer controlled_buffer_3
  assign controlled_buffer_4_out = rse ? {controlled_buffer_1_out_2[7:5], controlled_buffer_1_out[4]} : 4'bz;  // Controlled_Buffer controlled_buffer_4
  assign controlled_buffer_3_out = r1s ? {controlled_buffer_1_out_2[7:5], controlled_buffer_1_out[4]} : 4'bz;  // Controlled_Buffer controlled_buffer_5
  assign controlled_buffer_4_out = r1e ? {controlled_buffer_1_out_2[7:5], controlled_buffer_1_out[4]} : 4'bz;  // Controlled_Buffer controlled_buffer_6
  assign controlled_buffer_3_out = r2s ? controlled_buffer_1_out[3:0] : 4'bz;  // Controlled_Buffer controlled_buffer_7
  assign controlled_buffer_4_out = r2e ? controlled_buffer_1_out[3:0] : 4'bz;  // Controlled_Buffer controlled_buffer_8
  LED led_9 (.in(moe));
  LED led_10 (.in(iare));
  LED led_11 (.in(iars));
  LED led_12 (.in(as));
  LED led_13 (.in(be));
  Decoder #(.select(4)) decoder_1 (
    .out0(decoder_1_out0), .out1(decoder_1_out1), .out2(decoder_1_out2), .out3(or_6_out[3]),
    .out4(or_6_out[4]), .out5(or_6_out[5]), .out6(or_6_out[6]), .out7(or_6_out[7]), .out8(or_6_out[8]),
    .out9(or_6_out[9]), .out10(or_6_out[10]), .out11(or_6_out[11]), .out12(or_6_out[12]),
    .out13(or_6_out[13]), .out14(or_6_out[14]), .out15(or_6_out[15]), .sel(controlled_buffer_3_out),
    .en(or_2_out));
  or or_2 (or_2_out, rss, r1s, r2s);
  or or_3 (or_3_out, rse, r1e, r2e);
  Decoder #(.select(4)) decoder_2 (
    .out0(decoder_2_out0[0]), .out1(decoder_2_out1), .out2(decoder_2_out0[2]), .out3(decoder_2_out0[3]),
    .out4(decoder_2_out0[4]), .out5(decoder_2_out0[5]), .out6(decoder_2_out0[6]), .out7(decoder_2_out0[7]),
    .out8(decoder_2_out0[8]), .out9(decoder_2_out0[9]), .out10(decoder_2_out0[10]),
    .out11(decoder_2_out0[11]), .out12(decoder_2_out0[12]), .out13(decoder_2_out0[13]),
    .out14(decoder_2_out0[14]), .out15(decoder_2_out0[15]), .sel(controlled_buffer_4_out), .en(or_3_out));
  LED led_14 (.in(mos));
  LED led_15 (.in(mie));
  LED led_16 (.in(spe));
  LED led_17 (.in(spi));
  LED led_18 (.in(bs));
  LED led_19 (.in(r2e));
  or or_4 (or_6_out[2], ms, decoder_1_out2);
  or or_5 (decoder_2_out0[1], be, decoder_2_out1);
  LED led_20 (.in(mis));
  LED led_21 (.in(spc));
  LED led_22 (.in(r2s));
  or or_6 (or_6_out[0], as, decoder_1_out0);
  LED led_23 (.in(mae));
  LED led_24 (.in(mas));
  LED led_25 (.in(pce));
  LED led_26 (.in(pcs));
  LED led_27 (.in(r1e));
  LED led_28 (.in(r1s));
  or or_7 (or_6_out[1], bs, decoder_1_out1);
  LED led_29 (.in(raw));
  LED led_30 (.in(rar));
  LED led_31 (.in(pci));
  LED led_32 (.in(pcc));
  LED led_33 (.in(rse));
  LED led_34 (.in(rss));
  Pull_Resistor pull_resistor_1 (.node(iare));
  Pull_Resistor pull_resistor_2 (.node(iars));
  Pull_Resistor pull_resistor_3 (.node(spe));
  Pull_Resistor pull_resistor_4 (.node(spi));
  Pull_Resistor pull_resistor_5 (.node(afs));
  Pull_Resistor pull_resistor_6 (.node(spc));
  Pull_Resistor pull_resistor_7 (.node(pce));
  Pull_Resistor pull_resistor_8 (.node(pcs));
  Pull_Resistor pull_resistor_9 (.node(pci));
  Pull_Resistor pull_resistor_10 (.node(pcc));
  Pull_Resistor pull_resistor_11 (.node(moe));
  Pull_Resistor pull_resistor_12 (.node(mos));
  Pull_Resistor pull_resistor_13 (.node(mie));
  Pull_Resistor pull_resistor_14 (.node(mis));
  Pull_Resistor pull_resistor_15 (.node(mae));
  Pull_Resistor pull_resistor_16 (.node(mas));
  Pull_Resistor pull_resistor_17 (.node(raw));
  Pull_Resistor pull_resistor_18 (.node(rar));
  Register #(.trigger("high"), .width(16)) acc (
    .D(pull_resistor_59_node), .en(or_6_out[0]), .clk(xor_1_out), .Q(acc_q));  // open: clr
  Register #(.trigger("high"), .width(16)) alb (
    .D(controlled_buffer_9_out), .en(or_6_out[1]), .clk(xor_1_out), .Q(alb_q));  // open: clr
  Register #(.trigger("high"), .width(16)) muc (
    .D(multiplier_1_out), .en(or_6_out[2]), .clk(xor_1_out), .Q(muc_q));  // open: clr
  Register #(.trigger("high"), .width(16)) rdw (
    .D(controlled_buffer_9_out), .en(or_6_out[3]), .clk(xor_1_out), .Q({rdw_q_4, rdw_q_3, rdw_q_2, rdw_q}));  // open: clr
  Register #(.trigger("high"), .width(16)) rew (
    .D(controlled_buffer_9_out), .en(or_6_out[4]), .clk(xor_1_out), .Q({rew_q_4, rew_q_3, rew_q_2, rew_q}));  // open: clr
  Register #(.trigger("high"), .width(16)) rfw (
    .D(controlled_buffer_9_out), .en(or_6_out[5]), .clk(xor_1_out), .Q({rfw_q_4, rfw_q_3, rfw_q_2, rfw_q}));  // open: clr
  Register #(.trigger("high"), .width(16)) rgw (
    .D(controlled_buffer_9_out), .en(or_6_out[6]), .clk(xor_1_out), .Q({rgw_q_4, rgw_q_3, rgw_q_2, rgw_q}));  // open: clr
  Register #(.trigger("high"), .width(16)) rhw (
    .D(controlled_buffer_9_out), .en(or_6_out[7]), .clk(xor_1_out), .Q({rhw_q_4, rhw_q_3, rhw_q_2, rhw_q}));  // open: clr
  Register #(.trigger("high"), .width(16)) riw (
    .D(controlled_buffer_9_out), .en(or_6_out[8]), .clk(xor_1_out), .Q({riw_q_4, riw_q_3, riw_q_2, riw_q}));  // open: clr
  Register #(.trigger("high"), .width(16)) rjw (
    .D(controlled_buffer_9_out), .en(or_6_out[9]), .clk(xor_1_out), .Q({rjw_q_4, rjw_q_3, rjw_q_2, rjw_q}));  // open: clr
  Register #(.trigger("high"), .width(16)) rkw (
    .D(controlled_buffer_9_out), .en(or_6_out[10]), .clk(xor_1_out), .Q({rkw_q_4, rkw_q_3, rkw_q_2, rkw_q}));  // open: clr
  Register #(.trigger("high"), .width(16)) rlw (
    .D(controlled_buffer_9_out), .en(or_6_out[11]), .clk(xor_1_out), .Q({rlw_q_4, rlw_q_3, rlw_q_2, rlw_q}));  // open: clr
  Register #(.trigger("high"), .width(16)) rmw (
    .D(controlled_buffer_9_out), .en(or_6_out[12]), .clk(xor_1_out), .Q({rmw_q_4, rmw_q_3, rmw_q_2, rmw_q}));  // open: clr
  Register #(.trigger("high"), .width(16)) rnw (
    .D(controlled_buffer_9_out), .en(or_6_out[13]), .clk(xor_1_out), .Q({rnw_q_4, rnw_q_3, rnw_q_2, rnw_q}));  // open: clr
  Register #(.trigger("high"), .width(16)) rpw (
    .D(controlled_buffer_9_out), .en(or_6_out[14]), .clk(xor_1_out), .Q({rpw_q_4, rpw_q_3, rpw_q_2, rpw_q}));  // open: clr
  Register #(.trigger("high"), .width(16)) rqw (
    .D(controlled_buffer_9_out), .en(or_6_out[15]), .clk(xor_1_out), .Q({rqw_q_4, rqw_q_3, rqw_q_2, rqw_q}));  // open: clr
  assign controlled_buffer_9_out = decoder_2_out0[0] ? acc_q : 16'bz;  // Controlled_Buffer controlled_buffer_9
  assign controlled_buffer_10_out = decoder_2_out0[1] ? alb_q : 16'bz;  // Controlled_Buffer controlled_buffer_10
  assign controlled_buffer_9_out = decoder_2_out0[2] ? muc_q : 16'bz;  // Controlled_Buffer controlled_buffer_11
  assign controlled_buffer_9_out = decoder_2_out0[3] ? {rdw_q_4, rdw_q_3, rdw_q_2, rdw_q} : 16'bz;  // Controlled_Buffer controlled_buffer_12
  assign controlled_buffer_9_out = decoder_2_out0[4] ? {rew_q_4, rew_q_3, rew_q_2, rew_q} : 16'bz;  // Controlled_Buffer controlled_buffer_13
  assign controlled_buffer_9_out = decoder_2_out0[5] ? {rfw_q_4, rfw_q_3, rfw_q_2, rfw_q} : 16'bz;  // Controlled_Buffer controlled_buffer_14
  assign controlled_buffer_9_out = decoder_2_out0[6] ? {rgw_q_4, rgw_q_3, rgw_q_2, rgw_q} : 16'bz;  // Controlled_Buffer controlled_buffer_15
  assign controlled_buffer_9_out = decoder_2_out0[7] ? {rhw_q_4, rhw_q_3, rhw_q_2, rhw_q} : 16'bz;  // Controlled_Buffer controlled_buffer_16
  assign controlled_buffer_9_out = decoder_2_out0[8] ? {riw_q_4, riw_q_3, riw_q_2, riw_q} : 16'bz;  // Controlled_Buffer controlled_buffer_17
  assign controlled_buffer_9_out = decoder_2_out0[9] ? {rjw_q_4, rjw_q_3, rjw_q_2, rjw_q} : 16'bz;  // Controlled_Buffer controlled_buffer_18
  assign controlled_buffer_9_out = decoder_2_out0[10] ? {rkw_q_4, rkw_q_3, rkw_q_2, rkw_q} : 16'bz;  // Controlled_Buffer controlled_buffer_19
  assign controlled_buffer_9_out = decoder_2_out0[11] ? {rlw_q_4, rlw_q_3, rlw_q_2, rlw_q} : 16'bz;  // Controlled_Buffer controlled_buffer_20
  assign controlled_buffer_9_out = decoder_2_out0[12] ? {rmw_q_4, rmw_q_3, rmw_q_2, rmw_q} : 16'bz;  // Controlled_Buffer controlled_buffer_21
  assign controlled_buffer_9_out = decoder_2_out0[13] ? {rnw_q_4, rnw_q_3, rnw_q_2, rnw_q} : 16'bz;  // Controlled_Buffer controlled_buffer_22
  assign controlled_buffer_9_out = decoder_2_out0[14] ? {rpw_q_4, rpw_q_3, rpw_q_2, rpw_q} : 16'bz;  // Controlled_Buffer controlled_buffer_23
  assign controlled_buffer_9_out = decoder_2_out0[15] ? {rqw_q_4, rqw_q_3, rqw_q_2, rqw_q} : 16'bz;  // Controlled_Buffer controlled_buffer_24
  Pull_Resistor pull_resistor_19 (.node(pull_resistor_59_node[15]));
  Pull_Resistor pull_resistor_20 (.node(controlled_buffer_10_out[15]));
  Pull_Resistor pull_resistor_21 (.node(controlled_buffer_9_out[15]));
  Pull_Resistor pull_resistor_22 (.node(controlled_buffer_9_out[14]));
  Pull_Resistor pull_resistor_23 (.node(controlled_buffer_9_out[13]));
  Pull_Resistor pull_resistor_24 (.node(controlled_buffer_9_out[12]));
  Pull_Resistor pull_resistor_25 (.node(controlled_buffer_9_out[11]));
  Pull_Resistor pull_resistor_26 (.node(controlled_buffer_9_out[10]));
  Pull_Resistor pull_resistor_27 (.node(controlled_buffer_9_out[9]));
  Pull_Resistor pull_resistor_28 (.node(controlled_buffer_9_out[8]));
  Pull_Resistor pull_resistor_29 (.node(pull_resistor_59_node[14]));
  Pull_Resistor pull_resistor_30 (.node(pull_resistor_59_node[13]));
  Pull_Resistor pull_resistor_31 (.node(pull_resistor_59_node[12]));
  Pull_Resistor pull_resistor_32 (.node(pull_resistor_59_node[11]));
  Pull_Resistor pull_resistor_33 (.node(pull_resistor_59_node[10]));
  Pull_Resistor pull_resistor_34 (.node(pull_resistor_59_node[9]));
  Pull_Resistor pull_resistor_35 (.node(pull_resistor_59_node[8]));
  Pull_Resistor pull_resistor_36 (.node(pull_resistor_59_node[7]));
  Pull_Resistor pull_resistor_37 (.node(controlled_buffer_10_out[14]));
  Pull_Resistor pull_resistor_38 (.node(controlled_buffer_10_out[13]));
  Pull_Resistor pull_resistor_39 (.node(controlled_buffer_10_out[12]));
  Pull_Resistor pull_resistor_40 (.node(controlled_buffer_10_out[11]));
  Pull_Resistor pull_resistor_41 (.node(controlled_buffer_10_out[10]));
  Pull_Resistor pull_resistor_42 (.node(controlled_buffer_10_out[9]));
  Pull_Resistor pull_resistor_43 (.node(controlled_buffer_10_out[8]));
  Pull_Resistor pull_resistor_44 (.node(controlled_buffer_10_out[7]));
  Hex_Digit_Display #(.decimalPoint("false")) hex_digit_display_5 (.value(rdw_q_4));
  Hex_Digit_Display #(.decimalPoint("false")) hex_digit_display_6 (.value(rdw_q_3));
  Hex_Digit_Display #(.decimalPoint("false")) hex_digit_display_7 (.value(rew_q_4));
  Hex_Digit_Display #(.decimalPoint("false")) hex_digit_display_8 (.value(rew_q_3));
  Hex_Digit_Display #(.decimalPoint("false")) hex_digit_display_9 (.value(rfw_q_4));
  Hex_Digit_Display #(.decimalPoint("false")) hex_digit_display_10 (.value(rfw_q_3));
  Hex_Digit_Display #(.decimalPoint("false")) hex_digit_display_11 (.value(rgw_q_4));
  Hex_Digit_Display #(.decimalPoint("false")) hex_digit_display_12 (.value(rgw_q_3));
  Hex_Digit_Display #(.decimalPoint("false")) hex_digit_display_13 (.value(rhw_q_4));
  Hex_Digit_Display #(.decimalPoint("false")) hex_digit_display_14 (.value(rhw_q_3));
  Hex_Digit_Display #(.decimalPoint("false")) hex_digit_display_15 (.value(riw_q_4));
  Hex_Digit_Display #(.decimalPoint("false")) hex_digit_display_16 (.value(riw_q_3));
  Hex_Digit_Display #(.decimalPoint("false")) hex_digit_display_17 (.value(rjw_q_4));
  Hex_Digit_Display #(.decimalPoint("false")) hex_digit_display_18 (.value(rjw_q_3));
  Hex_Digit_Display #(.decimalPoint("false")) hex_digit_display_19 (.value(rkw_q_4));
  Hex_Digit_Display #(.decimalPoint("false")) hex_digit_display_20 (.value(rkw_q_3));
  Hex_Digit_Display #(.decimalPoint("false")) hex_digit_display_21 (.value(rlw_q_4));
  Hex_Digit_Display #(.decimalPoint("false")) hex_digit_display_22 (.value(rlw_q_3));
  Hex_Digit_Display #(.decimalPoint("false")) hex_digit_display_23 (.value(rmw_q_4));
  Hex_Digit_Display #(.decimalPoint("false")) hex_digit_display_24 (.value(rmw_q_3));
  Hex_Digit_Display #(.decimalPoint("false")) hex_digit_display_25 (.value(rnw_q_4));
  Hex_Digit_Display #(.decimalPoint("false")) hex_digit_display_26 (.value(rnw_q_3));
  Hex_Digit_Display #(.decimalPoint("false")) hex_digit_display_27 (.value(rpw_q_4));
  Hex_Digit_Display #(.decimalPoint("false")) hex_digit_display_28 (.value(rpw_q_3));
  Hex_Digit_Display #(.decimalPoint("false")) hex_digit_display_29 (.value(rqw_q_4));
  Hex_Digit_Display #(.decimalPoint("false")) hex_digit_display_30 (.value(rqw_q_3));
  Pull_Resistor pull_resistor_45 (.node(controlled_buffer_9_out[7]));
  Pull_Resistor pull_resistor_46 (.node(controlled_buffer_9_out[6]));
  Pull_Resistor pull_resistor_47 (.node(controlled_buffer_9_out[5]));
  Pull_Resistor pull_resistor_48 (.node(controlled_buffer_9_out[4]));
  Pull_Resistor pull_resistor_49 (.node(controlled_buffer_9_out[3]));
  Pull_Resistor pull_resistor_50 (.node(controlled_buffer_9_out[2]));
  Pull_Resistor pull_resistor_51 (.node(controlled_buffer_9_out[1]));
  Pull_Resistor pull_resistor_52 (.node(controlled_buffer_9_out[0]));
  // LedBar #(.inputtype("row"), .matrixcols(5)) ledbar_1: pin names not known; wires that end beside it: ledbar_1_p1
  Pull_Resistor pull_resistor_53 (.node(pull_resistor_59_node[6]));
  Pull_Resistor pull_resistor_54 (.node(pull_resistor_59_node[5]));
  Pull_Resistor pull_resistor_55 (.node(pull_resistor_59_node[4]));
  Pull_Resistor pull_resistor_56 (.node(pull_resistor_59_node[3]));
  Pull_Resistor pull_resistor_57 (.node(pull_resistor_59_node[2]));
  Pull_Resistor pull_resistor_58 (.node(pull_resistor_59_node[1]));
  Pull_Resistor pull_resistor_59 (.node(pull_resistor_59_node[0]));
  Pull_Resistor pull_resistor_60 (.node(controlled_buffer_10_out[6]));
  Pull_Resistor pull_resistor_61 (.node(controlled_buffer_10_out[5]));
  Pull_Resistor pull_resistor_62 (.node(controlled_buffer_10_out[4]));
  Pull_Resistor pull_resistor_63 (.node(controlled_buffer_10_out[3]));
  Pull_Resistor pull_resistor_64 (.node(controlled_buffer_10_out[2]));
  Pull_Resistor pull_resistor_65 (.node(controlled_buffer_10_out[1]));
  Pull_Resistor pull_resistor_66 (.node(controlled_buffer_10_out[0]));
  Hex_Digit_Display #(.decimalPoint("false")) hex_digit_display_31 (.value(rdw_q_2));
  Hex_Digit_Display #(.decimalPoint("false")) hex_digit_display_32 (.value(rdw_q));
  Hex_Digit_Display #(.decimalPoint("false")) hex_digit_display_33 (.value(rew_q_2));
  Hex_Digit_Display #(.decimalPoint("false")) hex_digit_display_34 (.value(rew_q));
  Hex_Digit_Display #(.decimalPoint("false")) hex_digit_display_35 (.value(rfw_q_2));
  Hex_Digit_Display #(.decimalPoint("false")) hex_digit_display_36 (.value(rfw_q));
  Hex_Digit_Display #(.decimalPoint("false")) hex_digit_display_37 (.value(rgw_q_2));
  Hex_Digit_Display #(.decimalPoint("false")) hex_digit_display_38 (.value(rgw_q));
  Hex_Digit_Display #(.decimalPoint("false")) hex_digit_display_39 (.value(rhw_q_2));
  Hex_Digit_Display #(.decimalPoint("false")) hex_digit_display_40 (.value(rhw_q));
  Hex_Digit_Display #(.decimalPoint("false")) hex_digit_display_41 (.value(riw_q_2));
  Hex_Digit_Display #(.decimalPoint("false")) hex_digit_display_42 (.value(riw_q));
  Hex_Digit_Display #(.decimalPoint("false")) hex_digit_display_43 (.value(rjw_q_2));
  Hex_Digit_Display #(.decimalPoint("false")) hex_digit_display_44 (.value(rjw_q));
  Hex_Digit_Display #(.decimalPoint("false")) hex_digit_display_45 (.value(rkw_q_2));
  Hex_Digit_Display #(.decimalPoint("false")) hex_digit_display_46 (.value(rkw_q));
  Hex_Digit_Display #(.decimalPoint("false")) hex_digit_display_47 (.value(rlw_q_2));
  Hex_Digit_Display #(.decimalPoint("false")) hex_digit_display_48 (.value(rlw_q));
  Hex_Digit_Display #(.decimalPoint("false")) hex_digit_display_49 (.value(rmw_q_2));
  Hex_Digit_Display #(.decimalPoint("false")) hex_digit_display_50 (.value(rmw_q));
  Hex_Digit_Display #(.decimalPoint("false")) hex_digit_display_51 (.value(rnw_q_2));
  Hex_Digit_Display #(.decimalPoint("false")) hex_digit_display_52 (.value(rnw_q));
  Hex_Digit_Display #(.decimalPoint("false")) hex_digit_display_53 (.value(rpw_q_2));
  Hex_Digit_Display #(.decimalPoint("false")) hex_digit_display_54 (.value(rpw_q));
  Hex_Digit_Display #(.decimalPoint("false")) hex_digit_display_55 (.value(rqw_q_2));
  Hex_Digit_Display #(.decimalPoint("false")) hex_digit_display_56 (.value(rqw_q));
  Register #(.trigger("high"), .width(5)) register_2 (
    .D(customcomparator_1_p8), .en(afs), .clk(afs), .Q(ledbar_1_p1));  // open: clr
  Register #(.trigger("high"), .width(16)) register_3 (
    .D(controlled_buffer_9_out), .en(iars), .clk(iars), .Q(register_3_q));  // open: clr
  Adder #(.width(16)) adder_1 (
    .a(controlled_buffer_9_out), .b(controlled_buffer_10_out), .out(adder_1_out),
    .cin(pull_resistor_67_node), .cout(adder_1_cout));
  Pull_Resistor pull_resistor_67 (.node(pull_resistor_67_node));
  Subtractor #(.width(16)) subtractor_1 (
    .a(controlled_buffer_9_out), .b(controlled_buffer_10_out), .out(subtractor_1_out),
    .bin(pull_resistor_67_node), .bout(subtractor_1_bout));
  or or_8 (or_8_out, adder_1_cout, subtractor_1_bout);
  Multiplier #(.width(16)) multiplier_1 (
    .a(controlled_buffer_9_out), .b(controlled_buffer_10_out), .out(multiplier_1_out),
    .cout(multiplier_1_cout));  // open: cin
  // customcomparator customcomparator_1: pin names not known; wires that end beside it: controlled_buffer_9_out, controlled_buffer_10_out, or_8_out, customcomparator_1_p8[4], customcomparator_1_p8[3], customcomparator_1_p8[2], customcomparator_1_p8[1], customcomparator_1_p8[0]
  assign and_11_out = controlled_buffer_9_out & controlled_buffer_10_out;  // AND_Gate and_11, 16 bits wide
  assign or_9_out = controlled_buffer_9_out | controlled_buffer_10_out;  // OR_Gate or_9, 16 bits wide
  assign xor_2_out = controlled_buffer_9_out ^ controlled_buffer_10_out;  // XOR_Gate xor_2, 16 bits wide
  assign not_2_out = ~controlled_buffer_9_out;  // NOT_Gate not_2, 16 bits wide
  Shifter #(.width(16)) shifter_1 (
    .in(controlled_buffer_9_out), .\dist (controlled_buffer_10_out[3:0]), .out(shifter_1_out));
  Shifter #(.shift("lr"), .width(16)) shifter_2 (
    .in(controlled_buffer_9_out), .\dist (controlled_buffer_10_out[3:0]), .out(shifter_2_out));
  Shifter #(.shift("rl"), .width(16)) shifter_3 (
    .in(controlled_buffer_9_out), .\dist (controlled_buffer_10_out[3:0]), .out(shifter_3_out));
  Shifter #(.shift("rr"), .width(16)) shifter_4 (
    .in(controlled_buffer_9_out), .\dist (controlled_buffer_10_out[3:0]), .out(shifter_4_out));
  Adder #(.width(16)) adder_2 (
    .a(controlled_buffer_9_out), .b({16{1'b0}}), .out(adder_2_out), .cin(1'b1));  // open: cout
  Subtractor #(.width(16)) subtractor_2 (
    .a(controlled_buffer_9_out), .b({16{1'b0}}), .out(subtractor_2_out), .bin(1'b1));  // open: bout
  assign {controlled_buffer_25_out_4, controlled_buffer_25_out_3, controlled_buffer_25_out_2, controlled_buffer_25_out} = iare ? register_3_q : 16'bz;  // Controlled_Buffer controlled_buffer_25
  Register #(.trigger("high"), .width(16)) register_4 (
    .D({controlled_buffer_25_out_4, controlled_buffer_25_out_3, controlled_buffer_25_out_2, controlled_buffer_25_out}),
    .en(mas), .clk(mas), .Q(register_4_q));  // open: clr
  Register #(.trigger("high"), .width(16)) register_5 (
    .D(controlled_buffer_9_out), .en(mis), .clk(mis), .Q(register_5_q));  // open: clr
  Counter #(.max('hffff), .width(16)) counter_4 (
    .load(pcs), .up(pci), .count(pcc), .clk(counter_2_q), .D(controlled_buffer_26_out), .Q(counter_4_q));  // open: clr, carry
  assign controlled_buffer_26_out = pcs ? {controlled_buffer_25_out_4, controlled_buffer_25_out_3, controlled_buffer_25_out_2, controlled_buffer_25_out} : 16'bz;  // Controlled_Buffer controlled_buffer_26
  Pull_Resistor pull_resistor_68 (.node(controlled_buffer_25_out_4[3]));
  Pull_Resistor pull_resistor_69 (.node(controlled_buffer_25_out_4[2]));
  Pull_Resistor pull_resistor_70 (.node(controlled_buffer_25_out_4[1]));
  assign controlled_buffer_27_out = mae ? register_4_q : 16'bz;  // Controlled_Buffer controlled_buffer_27
  RAM #(.addrWidth(16), .dataWidth(16), .trigger("high")) ram_1 (
    .addr(controlled_buffer_27_out), .we(raw), .oe(rar), .din(controlled_buffer_28_out), .dout(ram_1_dout));
  assign controlled_buffer_28_out = mie ? register_5_q : 16'bz;  // Controlled_Buffer controlled_buffer_28
  Multiplexer #(.select(4), .width(16)) multiplexer_1 (
    .in0(adder_1_out), .in1(subtractor_1_out), .in2(multiplier_1_cout), .in4(and_11_out), .in5(or_9_out),
    .in6(xor_2_out), .in7(not_2_out), .in8(shifter_1_out), .in9(shifter_2_out), .in10(shifter_3_out),
    .in11(shifter_4_out), .in12(adder_2_out), .in13(subtractor_2_out), .out(pull_resistor_59_node),
    .sel(controlled_buffer_1_out_3));  // open: in3, in14, in15
  Pull_Resistor pull_resistor_71 (.node(controlled_buffer_25_out_4[0]));
  Pull_Resistor pull_resistor_72 (.node(controlled_buffer_25_out_3[3]));
  Pull_Resistor pull_resistor_73 (.node(controlled_buffer_25_out_3[2]));
  Pull_Resistor pull_resistor_74 (.node(controlled_buffer_25_out_3[1]));
  Pull_Resistor pull_resistor_75 (.node(controlled_buffer_25_out_3[0]));
  Pull_Resistor pull_resistor_76 (.node(controlled_buffer_25_out_2[3]));
  Pull_Resistor pull_resistor_77 (.node(controlled_buffer_25_out_2[2]));
  Pull_Resistor pull_resistor_78 (.node(controlled_buffer_25_out_2[1]));
  Hex_Digit_Display #(.decimalPoint("false")) hex_digit_display_57 (.value(acc_q[15:12]));
  Hex_Digit_Display #(.decimalPoint("false")) hex_digit_display_58 (.value(acc_q[11:8]));
  Hex_Digit_Display #(.decimalPoint("false")) hex_digit_display_59 (.value(alb_q[15:12]));
  Hex_Digit_Display #(.decimalPoint("false")) hex_digit_display_60 (.value(alb_q[11:8]));
  Hex_Digit_Display #(.decimalPoint("false")) hex_digit_display_61 (.value(pull_resistor_59_node[15:12]));
  Hex_Digit_Display #(.decimalPoint("false")) hex_digit_display_62 (.value(pull_resistor_59_node[11:8]));
  Pull_Resistor pull_resistor_79 (.node(controlled_buffer_25_out_2[0]));
  Pull_Resistor pull_resistor_80 (.node(controlled_buffer_25_out[3]));
  Pull_Resistor pull_resistor_81 (.node(controlled_buffer_25_out[2]));
  Pull_Resistor pull_resistor_82 (.node(controlled_buffer_25_out[1]));
  Pull_Resistor pull_resistor_83 (.node(controlled_buffer_25_out[0]));
  Hex_Digit_Display #(.decimalPoint("false")) hex_digit_display_63 (.value(controlled_buffer_25_out_4));
  Hex_Digit_Display #(.decimalPoint("false")) hex_digit_display_64 (.value(controlled_buffer_25_out_3));
  assign {controlled_buffer_25_out_4, controlled_buffer_25_out_3, controlled_buffer_25_out_2, controlled_buffer_25_out} = pce ? counter_4_q : 16'bz;  // Controlled_Buffer controlled_buffer_29
  Hex_Digit_Display #(.decimalPoint("false")) hex_digit_display_65 (.value(acc_q[7:4]));
  Hex_Digit_Display #(.decimalPoint("false")) hex_digit_display_66 (.value(acc_q[3:0]));
  Hex_Digit_Display #(.decimalPoint("false")) hex_digit_display_67 (.value(alb_q[7:4]));
  Hex_Digit_Display #(.decimalPoint("false")) hex_digit_display_68 (.value(alb_q[3:0]));
  Hex_Digit_Display #(.decimalPoint("false")) hex_digit_display_69 (.value(pull_resistor_59_node[7:4]));
  Hex_Digit_Display #(.decimalPoint("false")) hex_digit_display_70 (.value(pull_resistor_59_node[3:0]));
  Hex_Digit_Display #(.decimalPoint("false")) hex_digit_display_71 (.value(controlled_buffer_25_out_2));
  Hex_Digit_Display #(.decimalPoint("false")) hex_digit_display_72 (.value(controlled_buffer_25_out));
  Counter #(.max('hf), .width(4)) counter_5 (
    .clr(1'b0), .load(1'b0), .up(spi), .count(spc), .clk(counter_2_q), .Q(counter_5_q));  // open: D, carry
  Hex_Digit_Display #(.decimalPoint("false")) hex_digit_display_73 (.value(controlled_buffer_9_out[15:12]));
  Register #(.trigger("high"), .width(16)) register_6 (
    .D(controlled_buffer_30_out), .en(mos), .clk(mos), .Q(register_6_q));  // open: clr
  assign controlled_buffer_30_out = rar ? ram_1_dout : 16'bz;  // Controlled_Buffer controlled_buffer_30
  Hex_Digit_Display #(.decimalPoint("false")) hex_digit_display_74 (.value(controlled_buffer_9_out[11:8]));
  Hex_Digit_Display #(.decimalPoint("false")) hex_digit_display_75 (.value(controlled_buffer_9_out[7:4]));
  assign controlled_buffer_9_out = moe ? register_6_q : 16'bz;  // Controlled_Buffer controlled_buffer_31
  assign {controlled_buffer_25_out_4, controlled_buffer_25_out_3, controlled_buffer_25_out_2, controlled_buffer_25_out} = spe ? {pull_resistor_84_node, counter_5_q} : 16'bz;  // Controlled_Buffer controlled_buffer_32
  Pull_Resistor pull_resistor_84 (.node(pull_resistor_84_node[4]));
  Pull_Resistor #(.pull(1)) pull_resistor_85 (.node(pull_resistor_84_node[5]));
  Pull_Resistor pull_resistor_86 (.node(pull_resistor_84_node[6]));
  Pull_Resistor #(.pull(1)) pull_resistor_87 (.node(pull_resistor_84_node[7]));
  Pull_Resistor pull_resistor_88 (.node(pull_resistor_84_node[8]));
  Pull_Resistor pull_resistor_89 (.node(pull_resistor_84_node[9]));
  Pull_Resistor pull_resistor_90 (.node(pull_resistor_84_node[10]));
  Pull_Resistor pull_resistor_91 (.node(pull_resistor_84_node[11]));
  Pull_Resistor pull_resistor_92 (.node(pull_resistor_84_node[12]));
  Pull_Resistor pull_resistor_93 (.node(pull_resistor_84_node[13]));
  Pull_Resistor pull_resistor_94 (.node(pull_resistor_84_node[14]));
  Pull_Resistor pull_resistor_95 (.node(pull_resistor_84_node[15]));
  Hex_Digit_Display #(.decimalPoint("false")) hex_digit_display_76 (.value(controlled_buffer_9_out[3:0]));

  // Notes on the sheet:
  //   Clock Pulse Generator
  //   contents of Rom_MemoryControl (hex, n*v repeats v):
  //   4 49 80 4 49 80 4 49 80 7*0 4 49 80 4 49 80 4 10 2a 7*0 4 49 80 4 49 80 10*0 4 49 80 13*0 4 49 80 4
  //   49 80 10*0 4 49 80 13*0 4 49 80 4 49 80 4 10 2a 7*0 4 49 80 4 49 80 4 49 80 7*0 4 49 80 4 10 2a 10*0
  //   4 49 80 4 49 80 10*0 4 49 80 13*0 4 49 80 13*0 4 49 80 13*0 4 49 80 13*0 4 49 80 13*0 4 49 80 13*0 4
  //   49 80 13*0 4 49 80 13*0 4 49 80 13*0 4 49 80 13*0 4 49 80 13*0 4 49 80 13*0 4 49 80 13*0 4 49 80
  //   13*0 4 49 80 13*0 4 49 80 13*0 4 49 80 13*0 4 49 80 13*0 4 49 80 13*0 4 49 80 13*0 4 49 80 13*0 4 49
  //   80 13*0 4 49 80 4 49 80 4 49 80 7*0 4 49 80 4 49 80 4 10 2a 7*0 4 49 80 4 49 80 10*0 4 49 80 13*0 4
  //   49 80 4 49 80 10*0 4 49 80 4 49 80 10*0 4 49 80 4 49 80 4 10 2a 7*0 4 49 80 4 49 80 4 49 80 7*0 4 49
  //   80 4 10 2a 10*0 4 49 80 4 49 80 10*0 4 49 80 13*0 4 49 80 13*0 4 49 80 13*0 4 49 80 13*0 4 49 80
  //   13*0 4 49 80 13*0 4 49 80 13*0 4 49 80 13*0 4 49 80 13*0 4 49 80 13*0 4 49 80 13*0 4 49 80 13*0 4 49
  //   80 13*0 4 49 80 13*0 4 49 80 13*0 4 49 80 13*0 4 49 80 13*0 4 49 80 13*0 4 49 80 13*0 4 49 80 13*0 4
  //   49 80 13*0 4 49 80
  //   contents of Rom_CounterControl (hex, n*v repeats v):
  //   8 0 0 b 0 80 100 8*0 3 8 0 0 b 0 80 100 8*0 3 8 0 0 b 11*0 3 8 14*0 3 8 0 0 b 0 80 104 9*0 8 15*0 8
  //   0 0 b 0 80 100 8*0 3 8 0 0 b 0 80 100 8*0 3 8 0 0 40 30 10*0 3 8 0 0 40 10 10*0 3 8 14*0 3 8 14*0 3
  //   8 14*0 3 8 14*0 3 8 14*0 3 8 14*0 3 8 0 0 0 200 10*0 3 8 0 0 0 200 10*0 3 8 0 0 0 200 10*0 3 8 0 0 0
  //   200 10*0 3 8 0 0 0 200 10*0 3 8 0 0 0 200 10*0 3 8 0 0 0 200 10*0 3 8 0 0 0 200 10*0 3 8 0 0 0 200
  //   10*0 3 8 0 0 0 200 10*0 3 8 0 0 0 200 10*0 3 8 0 0 0 200 10*0 3 8 0 0 0 200 10*0 3 8 0 0 0 200 10*0
  //   3 8 0 0 0 200 10*0 3 8 0 0 0 200 10*0 3 8 0 0 b 0 80 100 8*0 3 8 0 0 b 0 80 100 8*0 3 8 0 0 b 11*0 3
  //   8 14*0 3 8 0 0 b 0 80 104 9*0 8 0 0 b 0 80 104 9*0 8 0 0 b 0 80 100 8*0 3 8 0 0 b 0 80 100 8*0 3 8 0
  //   0 40 30 10*0 3 8 0 0 40 10 10*0 3 8 14*0 3 8 14*0 3 8 14*0 3 8 14*0 3 8 14*0 3 8 14*0 3 8 0 0 0 200
  //   10*0 3 8 0 0 0 200 10*0 3 8 0 0 0 200 10*0 3 8 0 0 0 200 10*0 3 8 0 0 0 200 10*0 3 8 0 0 0 200 10*0
  //   3 8 0 0 0 200 10*0 3 8 0 0 0 200 10*0 3 8 0 0 0 200 10*0 3 8 0 0 0 200 10*0 3 8 0 0 0 200 10*0 3 8 0
  //   0 0 200 10*0 3 8 0 0 0 200 10*0 3 8 0 0 0 200 10*0 3 8 0 0 0 200 10*0 3 8 0 0 0 200 10*0 3
  //   contents of Rom_RegisterControl (hex, n*v repeats v):
  //   8*0 1 14*0 2 13*0 1 13*0 18 80*0 2 16*0 1 109*0 60 188 14*0 60 188 14*0 60 388 14*0 60 188 14*0 60
  //   188 14*0 60 188 14*0 60 188 14*0 60 188 14*0 60 188 14*0 60 188 14*0 60 188 14*0 60 188 14*0 60 188
  //   14*0 60 188 14*0 60 188 14*0 60 188 19*0 1 14*0 2 13*0 1 13*0 18 80*0 2 16*0 1 109*0 60 188 14*0 60
  //   188 14*0 60 388 14*0 60 188 14*0 60 188 14*0 60 188 14*0 60 188 14*0 60 188 14*0 60 188 14*0 60 188
  //   14*0 60 188 14*0 60 188 14*0 60 188 14*0 60 188 14*0 60 188 14*0 60 188
  //   contents of Rom_PeripheralControl (hex, n*v repeats v):
  //   8*0 1 14*0 2 16*0 1 10*0 18 80*0 2 16*0 1 109*0 60 188 14*0 60 188 14*0 60 388 14*0 60 188 14*0 60
  //   188 14*0 60 188 14*0 60 188 14*0 60 188 14*0 60 188 14*0 60 188 14*0 60 188 14*0 60 188 14*0 60 188
  //   14*0 60 188 14*0 60 188 14*0 60 188 19*0 1 14*0 2 16*0 1 10*0 18 80*0 2 16*0 1 109*0 60 188 14*0 60
  //   188 14*0 60 388 14*0 60 188 14*0 60 188 14*0 60 188 14*0 60 188 14*0 60 188 14*0 60 188 14*0 60 188
  //   14*0 60 188 14*0 60 188 14*0 60 188 14*0 60 188 14*0 60 188 14*0 60 188
  //   Register Bank
  //   Arithmetic & Logic Unit
  //   Memory Unit
endmodule

module customcomparator (
  input  CarryBorrow,
  input  [15:0] Input_A,
  input  [15:0] Input_B,
  output Carry,
  output A_Lgr,
  output Equal,
  output A_Zro,
  output A_Neg
);

  wire or_1_out;

  Comparator #(.mode("unsigned"), .width(16)) comparator_1 (
    .a(Input_A), .b(Input_B), .gt(A_Lgr), .eq(Equal));  // open: lt
  Comparator #(.mode("unsigned"), .width(16)) comparator_2 (.a(Input_A), .b({16{1'b0}}), .lt(A_Neg));  // open: gt, eq
  not not_1 (A_Zro, or_1_out);
  or or_1 (or_1_out, Input_A[0], Input_A[1], Input_A[2], Input_A[3], Input_A[4], Input_A[5], Input_A[6], Input_A[7], Input_A[9], Input_A[10], Input_A[11], Input_A[12], Input_A[13], Input_A[14], Input_A[15], Input_A[8]);

  assign Carry = CarryBorrow;
endmodule
